// Digital circuit stackerproto3ntb.dig as structural Verilog
module stackerproto3ntb (
);

  wire ALU_BUS_out, CLOCK_out, d_ff_as_1_q, dipswitch_9_out, dipswitch_10_out, dipswitch_11_out,
       dipswitch_12_out, dipswitch_13_out, dipswitch_14_out, ENABLE_out, RESET_out, ssalu8b_1_co,
       ssalu8b_1_z, STKDIR_out, XEN_out;
  wire [7:0] creg8_1_q, demultiplexer_1_out_0, demultiplexer_1_out_1, dipswitch_8_out, driver_1_out,
       driver_2_out, multiplexer_1_out, od8x8bsrfv2_1_sro, od8x8bsrfv2_1_top, ssalu8b_1_y;

  Button RESET (.out(RESET_out));
  Button CLOCK (.out(CLOCK_out));
  DipSwitch ALU_BUS (.out(ALU_BUS_out));
  DipSwitch XEN (.out(XEN_out));
  DipSwitch STKDIR (.out(STKDIR_out));
  DipSwitch ENABLE (.out(ENABLE_out));
  Multiplexer #(.Bits(8)) multiplexer_1 (
    .sel(ALU_BUS_out), .in_0(driver_1_out), .in_1(ssalu8b_1_y), .out(multiplexer_1_out));
  DipSwitch dipswitch_1 (.out(dipswitch_8_out[0]));
  DipSwitch dipswitch_2 (.out(dipswitch_8_out[1]));
  DipSwitch dipswitch_3 (.out(dipswitch_8_out[2]));
  DipSwitch dipswitch_4 (.out(dipswitch_8_out[3]));
  DipSwitch dipswitch_5 (.out(dipswitch_8_out[4]));
  DipSwitch dipswitch_6 (.out(dipswitch_8_out[5]));
  DipSwitch dipswitch_7 (.out(dipswitch_8_out[6]));
  DipSwitch dipswitch_8 (.out(dipswitch_8_out[7]));
  DipSwitch dipswitch_9 (.out(dipswitch_9_out));
  DipSwitch dipswitch_10 (.out(dipswitch_10_out));
  assign driver_1_out = dipswitch_10_out ? driver_2_out : 8'bz;  // Driver driver_1
  assign driver_2_out = dipswitch_9_out ? dipswitch_8_out : 8'bz;  // Driver driver_2
  Seven_Seg_Hex seven_seg_hex_1 (.d(driver_2_out[7:4]), .dp(1'b0));
  // Probe on od8x8bsrfv2_1_top
  od8x8bsrfV2 od8x8bsrfv2_1 (
    .SRI(multiplexer_1_out), .DIR(STKDIR_out), .EN(ENABLE_out), .CLK(CLOCK_out), .RST(RESET_out),
    .RSI({8{1'b0}}), .SRO(od8x8bsrfv2_1_sro), .TOP(od8x8bsrfv2_1_top));  // open: CPT, DPT
  Seven_Seg_Hex seven_seg_hex_2 (.d(driver_2_out[3:0]), .dp(1'b0));
  DipSwitch dipswitch_11 (.out(dipswitch_11_out));
  Demultiplexer #(.Bits(8)) demultiplexer_1 (
    .sel(ALU_BUS_out), .in(od8x8bsrfv2_1_top), .out_0(demultiplexer_1_out_0), .out_1(demultiplexer_1_out_1));
  assign driver_2_out = dipswitch_11_out ? demultiplexer_1_out_0 : 8'bz;  // Driver driver_3
  CREG8 creg8_1 (.D(demultiplexer_1_out_1), .R(RESET_out), .CLK(CLOCK_out), .EN(XEN_out), .Q(creg8_1_q));
  // Probe on od8x8bsrfv2_1_sro
  // Probe on creg8_1_q
  DipSwitch dipswitch_12 (.out(dipswitch_12_out));
  DipSwitch dipswitch_13 (.out(dipswitch_13_out));
  DipSwitch dipswitch_14 (.out(dipswitch_14_out));
  SSALU8B ssalu8b_1 (
    .A(demultiplexer_1_out_1), .X(creg8_1_q), .OP0(dipswitch_12_out), .OP1(dipswitch_13_out),
    .ALT(dipswitch_14_out), .CO(ssalu8b_1_co), .CIN(d_ff_as_1_q), .Y(ssalu8b_1_y), .Z(ssalu8b_1_z));
  D_FF_AS d_ff_as_1 (.Set(1'b0), .D(ssalu8b_1_co), .C(CLOCK_out), .Clr(RESET_out), .Q(d_ff_as_1_q));  // open: nQ
  // Probe on ssalu8b_1_y
  LED led_1 (.in(ssalu8b_1_z));
endmodule
